// Logisim project s-mips.circ as structural Verilog: 15 circuits, main circuit S-MIPS Board
module S_MIPS_Board (
  input  DESHABILITAR_DISPATCHER,
  output halt
);

  wire button_1_out, CLK, CS, d_ff_1_q, LCLR, LoadRAM, LoadRAMOn, LW, R_R_W, R_W, ram_dispatcher_1_finished,
       RCS, Reset_out, RST, TTY_EN;
  wire [2:0] KDB;
  wire [3:0] LMask, Mask, ram_1_read_time, ram_1_write_time, RMask;
  wire [6:0] KDB_DATA, TTY_DATA;
  wire [15:0] Addr, LAddr, RAddr;
  wire [31:0] I0, I1, I2, I3, LData, ram_1_data_out_0, ram_1_data_out_1, ram_1_data_out_2, ram_1_data_out_3,
       RI0, RI1, RI2, RI3;

  TTY #(.rows(25), .cols(80)) tty_1 (.data(TTY_DATA), .clk(CLK), .we(TTY_EN), .clr(RST));
  not not_1 (LoadRAMOn, ram_dispatcher_1_finished);
  RAM_Dispatcher ram_dispatcher_1 (
    .WriteTime(ram_1_write_time), .Clock(CLK), .Data(LData), .Address(LAddr), .Mask(LMask),
    .Finished(ram_dispatcher_1_finished), .Write(LW), .CLR(LCLR));
  Keyboard #(.buflen(64)) keyboard_1 (.clk(CLK), .re(KDB[0]), .avail(KDB[2]), .data(KDB_DATA));  // open: clr
  RAM ram_1 (
    .Address(RAddr), .Data_Out_0(ram_1_data_out_0), .Data_Out_1(ram_1_data_out_1),
    .Data_Out_2(ram_1_data_out_2), .Data_Out_3(ram_1_data_out_3), .Data_In_0(RI0), .Data_In_1(RI1),
    .Data_In_2(RI2), .Data_In_3(RI3), .Mask(RMask), .nRead_Write(R_R_W), .Chip_Select(RCS),
    .Read_Time(ram_1_read_time), .Reset(button_1_out), .Write_Time(ram_1_write_time));
  Button button_1 (.out(button_1_out));
  D_Flip_Flop d_ff_1 (.clk(CLK), .D(1'b1), .Q(d_ff_1_q), .reset(Reset_out));  // open: Qn, preset, en
  Button Reset (.out(Reset_out));
  S_MIPS s_mips_1 (
    .Kbd_Enable(KDB[0]), .Address(Addr), .Kbd_Clear(KDB[1]), .Kbd_Available(KDB[2]), .RAM_In_0(I0),
    .Kbd_ASCII_Data(KDB_DATA), .RAM_In_1(I1), .TTY_Enable(TTY_EN), .RAM_In_2(I2), .RAM_In_3(I3),
    .TTY_ASCII_Data(TTY_DATA), .Reset(RST), .RAM_Out_0(ram_1_data_out_0), .Clock(CLK),
    .RAM_Out_1(ram_1_data_out_1), .Stop(halt), .RAM_Out_2(ram_1_data_out_2), .RAM_Out_3(ram_1_data_out_3),
    .Mask(Mask), .Read_Time(ram_1_read_time), .Write_Time(ram_1_write_time), .nRead_Write(R_W),
    .Chip_Select(CS));  // open: Output
  D_Flip_Flop d_ff_2 (.clk(CLK), .D(d_ff_1_q), .Qn(LCLR), .reset(Reset_out));  // open: Q, preset, en
  or or_1 (RST, LCLR, LoadRAM);
  Clock clock_1 (.out(CLK));
  Multiplexer #(.width(32), .enable("false")) multiplexer_1 (.in0(I0), .in1(LData), .out(RI0), .sel(LoadRAM));
  Multiplexer #(.width(32), .enable("false")) multiplexer_2 (.in0(I1), .in1(LData), .out(RI1), .sel(LoadRAM));
  Multiplexer #(.width(32), .enable("false")) multiplexer_3 (.in0(I2), .in1(LData), .out(RI2), .sel(LoadRAM));
  Multiplexer #(.width(32), .enable("false")) multiplexer_4 (.in0(I3), .in1(LData), .out(RI3), .sel(LoadRAM));
  and and_1 (LoadRAM, ~DESHABILITAR_DISPATCHER, LoadRAMOn);  // AND_Gate
  Multiplexer #(.width(16), .enable("false")) multiplexer_5 (.in0(Addr), .in1(LAddr), .out(RAddr), .sel(LoadRAM));
  Multiplexer #(.width(4), .enable("false")) multiplexer_6 (.in0(Mask), .in1(LMask), .out(RMask), .sel(LoadRAM));
  Multiplexer #(.enable("false")) multiplexer_7 (.in0(CS), .in1(LW), .out(RCS), .sel(LoadRAM));
  Multiplexer #(.enable("false")) multiplexer_8 (.in0(R_W), .in1(LW), .out(R_R_W), .sel(LoadRAM));

  // Notes on the sheet:
  //   NO MODIFICAR
  //   Keyboard
endmodule

module RAM (
  input  [15:0] Address,
  input  [31:0] Data_In_0,
  input  [31:0] Data_In_1,
  input  [31:0] Data_In_2,
  input  [31:0] Data_In_3,
  input  [3:0] Mask,
  input  nRead_Write,
  input  Chip_Select,
  input  Reset,
  output [31:0] Data_Out_0,
  output [31:0] Data_Out_1,
  output [31:0] Data_Out_2,
  output [31:0] Data_Out_3,
  output [3:0] Read_Time,
  output [3:0] Write_Time
);

  wire and_2_out, and_3_out, and_4_out, and_5_out, and_6_out, and_7_out, and_8_out, and_9_out, Changed, CLK,
       comparator_2_eq, comparator_3_eq, comparator_4_eq, comparator_5_eq, comparator_6_eq, Count,
       demultiplexer_3_out0, Idle, Idle_q, Load, Load0, Load1, nand_1_out, or_1_out, or_2_out, or_3_out,
       or_4_out, or_5_out, or_6_out, or_7_out, or_8_out, or_9_out, or_10_out, Proc_q, Update_Mem, Zero_Time;
  wire [3:0] counter_1_q, multiplexer_1_out, subtractor_1_out;
  wire [31:0] register_1_q, register_2_q, register_3_q, register_4_q, register_5_q;

  // Probe on 4'b0010
  // Probe on 4'b0010
  Multiplexer #(.width(4), .enable("false")) multiplexer_1 (
    .in0(4'b0010), .in1(4'b0010), .out(multiplexer_1_out), .sel(nRead_Write));
  or or_1 (or_1_out, Idle, Update_Mem);
  or or_2 (or_2_out, ~Chip_Select, Reset);  // OR_Gate
  Subtractor #(.width(4)) subtractor_1 (.a(multiplexer_1_out), .b(4'b0010), .out(subtractor_1_out));  // open: bin, bout
  Demultiplexer #(.enable("false")) demultiplexer_1 (.out0(Idle), .out1(Load0), .in(Idle_q), .sel(Changed));
  D_Flip_Flop u_Idle (.clk(CLK), .D(or_1_out), .Q(Idle_q), .preset(or_2_out));  // open: Qn, en, reset
  // Probe on counter_1_q
  Counter #(.width(4), .max('hf)) counter_1 (
    .load(Load), .D(subtractor_1_out), .count(Count), .Q(counter_1_q), .clk(CLK), .clr(or_3_out));  // open: carry
  or or_3 (or_3_out, ~Chip_Select, Reset);  // OR_Gate
  Comparator #(.width(4), .mode("unsigned")) comparator_1 (
    .a(4'b0000), .b(counter_1_q), .eq(Zero_Time));  // open: gt, lt
  or or_4 (or_4_out, Count, Load0, Load1);
  Register #(.width(32)) register_1 (.D(Data_In_0), .en(Chip_Select), .Q(register_1_q), .clk(CLK), .clr(or_5_out));
  or or_5 (or_5_out, ~Chip_Select, Reset);  // OR_Gate
  Register #(.width(32)) register_2 (.D(Data_In_1), .en(Chip_Select), .Q(register_2_q), .clk(CLK), .clr(or_6_out));
  or or_6 (or_6_out, ~Chip_Select, Reset);  // OR_Gate
  Register #(.width(32)) register_3 (.D(Data_In_2), .en(Chip_Select), .Q(register_3_q), .clk(CLK), .clr(or_7_out));
  or or_7 (or_7_out, ~Chip_Select, Reset);  // OR_Gate
  Register #(.width(32)) register_4 (.D(Data_In_3), .en(Chip_Select), .Q(register_4_q), .clk(CLK), .clr(or_8_out));
  or or_8 (or_8_out, ~Chip_Select, Reset);  // OR_Gate
  Register #(.width(32)) register_5 (
    .D({{11{1'b1}}, nRead_Write, Mask, Address}), .en(Chip_Select), .Q(register_5_q), .clk(CLK),
    .clr(or_9_out));
  or or_9 (or_9_out, ~Chip_Select, Reset);  // OR_Gate
  D_Flip_Flop Proc (.clk(CLK), .D(or_4_out), .Q(Proc_q), .reset(or_10_out));  // open: Qn, preset, en
  or or_10 (or_10_out, ~Chip_Select, Reset);  // OR_Gate
  Demultiplexer #(.enable("false")) demultiplexer_2 (
    .out0(Count), .out1(Update_Mem), .in(demultiplexer_3_out0), .sel(Zero_Time));
  Demultiplexer #(.enable("false")) demultiplexer_3 (
    .out0(demultiplexer_3_out0), .out1(Load1), .in(Proc_q), .sel(Changed));
  Clock clock_1 (.out(CLK));
  Comparator #(.width(32)) comparator_2 (.a(register_1_q), .b(Data_In_0), .eq(comparator_2_eq));  // open: gt, lt
  Comparator #(.width(32)) comparator_3 (.a(register_2_q), .b(Data_In_1), .eq(comparator_3_eq));  // open: gt, lt
  Comparator #(.width(32)) comparator_4 (.a(register_3_q), .b(Data_In_2), .eq(comparator_4_eq));  // open: gt, lt
  Comparator #(.width(32)) comparator_5 (.a(register_4_q), .b(Data_In_3), .eq(comparator_5_eq));  // open: gt, lt
  Comparator #(.width(32)) comparator_6 (
    .a(register_5_q), .b({{11{1'b1}}, nRead_Write, Mask, Address}), .eq(comparator_6_eq));  // open: gt, lt
  nand nand_1 (nand_1_out, comparator_6_eq, comparator_2_eq, comparator_3_eq, comparator_4_eq, comparator_5_eq);
  and and_1 (Changed, nand_1_out, Chip_Select);
  or or_11 (Load, Count, Load1, Load0);
  and and_2 (and_2_out, Mask[0], Update_Mem, nRead_Write);
  and and_3 (and_3_out, Mask[1], Update_Mem, nRead_Write);
  and and_4 (and_4_out, Mask[2], Update_Mem, nRead_Write);
  and and_5 (and_5_out, Mask[3], Update_Mem, nRead_Write);
  RAM_part #(.addrWidth(16), .dataWidth(32), .bus("separate")) ram_1 (
    .addr(Address), .din(Data_In_0), .data(Data_Out_0), .str(and_2_out), .sel(Chip_Select), .clk(CLK),
    .ld(and_6_out), .clr(Reset));
  and and_6 (and_6_out, ~nRead_Write, Idle);  // AND_Gate
  RAM_part #(.addrWidth(16), .dataWidth(32), .bus("separate")) ram_2 (
    .addr(Address), .din(Data_In_1), .data(Data_Out_1), .str(and_3_out), .sel(Chip_Select), .clk(CLK),
    .ld(and_7_out), .clr(Reset));
  and and_7 (and_7_out, ~nRead_Write, Idle);  // AND_Gate
  RAM_part #(.addrWidth(16), .dataWidth(32), .bus("separate")) ram_3 (
    .addr(Address), .din(Data_In_2), .data(Data_Out_2), .str(and_4_out), .sel(Chip_Select), .clk(CLK),
    .ld(and_8_out), .clr(Reset));
  and and_8 (and_8_out, ~nRead_Write, Idle);  // AND_Gate
  RAM_part #(.addrWidth(16), .dataWidth(32), .bus("separate")) ram_4 (
    .addr(Address), .din(Data_In_3), .data(Data_Out_3), .str(and_5_out), .sel(Chip_Select), .clk(CLK),
    .ld(and_9_out), .clr(Reset));
  and and_9 (and_9_out, ~nRead_Write, Idle);  // AND_Gate

  assign Read_Time = 4'b0010;
  assign Write_Time = 4'b0010;

  // Other names for the same wires on the sheet: M0 = Mask[0]; M1 = Mask[1]; M2 = Mask[2]; M3 = Mask[3];
  //   RW = nRead_Write; CLR = Reset; CS = Chip_Select; Load2 = Count

  // Notes on the sheet:
  //   NO MODIFICAR
  //   excepto quizás los valores RT y WT
  //   BANK0
  //   BANK1
  //   BANK2
  //   BANK3
endmodule

module S_MIPS (
  input  Kbd_Available,
  input  [31:0] RAM_Out_0,
  input  [6:0] Kbd_ASCII_Data,
  input  [31:0] RAM_Out_1,
  input  [31:0] RAM_Out_2,
  input  Reset,
  input  Clock,
  input  [31:0] RAM_Out_3,
  input  [3:0] Read_Time,
  input  [3:0] Write_Time,
  output [15:0] Address,
  output Kbd_Enable,
  output Kbd_Clear,
  output TTY_Enable,
  output [6:0] TTY_ASCII_Data,
  output Stop,
  output [31:0] Output,
  output [31:0] RAM_In_0,
  output [31:0] RAM_In_1,
  output [31:0] RAM_In_2,
  output [31:0] RAM_In_3,
  output [3:0] Mask,
  output nRead_Write,
  output Chip_Select
);

  wire and_1_out, beq, beq_en, bgtz, bgtz_en, blez, blez_en, bltz, bltz_en, bne, bne_en, comparator_1_gt,
       comparator_1_lt, comparator_2_eq, d_ff_4_q, d_ff_6_q, d_ff_7_q, d_ff_8_q, d_ff_9_q,
       demultiplexer_1_out0, demultiplexer_1_out1, demultiplexer_2_out0, demultiplexer_3_out0,
       demultiplexer_3_out1, demultiplexer_3_out2, demultiplexer_3_out3, demultiplexer_3_out4,
       demultiplexer_3_out5, demultiplexer_3_out6, demultiplexer_3_out7, demultiplexer_4_out0,
       demultiplexer_5_out0, demultiplexer_6_out0, demultiplexer_8_out0, demultiplexer_9_out0,
       demultiplexer_9_out1, enable_RF, enable_RF0, enable_RF1, enableHi_Lo, end_ram_operation, Hi_Lo_on,
       IDLE_q, IF, instruction_ready, is_halt, jmp, jr, l_PC, lw, not_1_out, not_2_out, not_3_out, not_4_out,
       or_1_out, or_2_out, or_3_out, or_4_out, or_5_out, or_6_out, or_7_out, or_8_out, or_9_out, or_10_out,
       or_11_out, or_12_out, or_13_out, or_14_out, or_16_out, or_18_out, pop, push, reset_IR, RW1, sp_enable,
       sp_enable0, sp_enable1, start_RAM_op0, start_RAM_op2, sw_t, tty, wait_q;
  wire [1:0] Hi_Lo_op;
  wire [2:0] ALU_OP, branch, dISel;
  wire [4:0] SA, SB, SW;
  wire [25:0] direction;
  wire [31:0] A, adder_1_out, adder_2_out, ALU_result, B, bit_extender_1_out, current_PC, High, IR, K, Low,
       multiplexer_1_out, multiplexer_2_out, multiplexer_4_out, multiplexer_5_out, multiplexer_6_out,
       multiplexer_7_out, multiplexer_8_out, multiplexer_9_out, RAM_OUT, RAM_WRITE, random_1_out, SP;
  wire [31:7] controlled_buffer_1_out;

  D_Flip_Flop IDLE (.clk(Clock), .D(demultiplexer_1_out0), .Q(IDLE_q), .preset(Reset));  // open: Qn, en, reset
  not not_1 (not_1_out, Reset);
  not not_2 (not_2_out, Stop);
  Demultiplexer #(.enable("false")) demultiplexer_1 (
    .out0(demultiplexer_1_out0), .out1(demultiplexer_1_out1), .in(IDLE_q), .sel(not_3_out));
  not not_3 (not_3_out, Reset);
  Counter #(.width(32), .max('hffffffff)) counter_1 (
    .count(and_1_out), .Q(Output), .clk(Clock));  // open: load, D, carry, clr
  and and_1 (and_1_out, not_1_out, not_2_out);
  or or_1 (or_1_out, reset_IR, demultiplexer_1_out1);
  D_Flip_Flop start_reading_instruction (
    .clk(Clock), .D(or_1_out), .Q(start_RAM_op0), .reset(Reset));  // open: Qn, preset, en
  or or_2 (or_2_out, lw, sw_t);
  Multiplexer #(.width(32), .enable("false")) multiplexer_1 (
    .in0(current_PC), .in1(ALU_result), .out(multiplexer_1_out), .sel(or_2_out));
  or or_3 (or_3_out, push, pop);
  Multiplexer #(.width(32), .enable("false")) multiplexer_2 (
    .in0(multiplexer_1_out), .in1(SP), .out(multiplexer_2_out), .sel(or_3_out));
  or or_4 (or_4_out, wait_q, start_RAM_op0);
  hi_lo hi_lo_1 (
    .A(A), .B(B), .clk(Clock), .rst(Reset), .op_selector(Hi_Lo_op), .enable(enableHi_Lo), .Low(Low),
    .High(High));
  Register #(.width(32)) InstructionRegister (.D(RAM_OUT), .en(instruction_ready), .Q(IR), .clk(Clock), .clr(or_5_out));
  or or_5 (or_5_out, Reset, reset_IR);
  Demultiplexer #(.enable("false")) demultiplexer_2 (
    .out0(demultiplexer_2_out0), .out1(instruction_ready), .in(or_4_out), .sel(end_ram_operation));
  buf or_6 (or_6_out, RW1);  // OR_Gate
  or or_7 (or_7_out, start_RAM_op2, RW1, start_RAM_op0);
  assign {controlled_buffer_1_out, TTY_ASCII_Data} = tty ? A : 32'bz;  // Controlled_Buffer controlled_buffer_1
  D_Flip_Flop \wait  (.clk(Clock), .D(demultiplexer_2_out0), .Q(wait_q), .reset(Reset));  // open: Qn, preset, en
  Multiplexer #(.width(32), .enable("false")) multiplexer_3 (
    .in0(A), .in1(B), .out({RAM_WRITE[7:0], RAM_WRITE[15:8], RAM_WRITE[23:16], RAM_WRITE[31:24]}), .sel(sw_t));
  D_Flip_Flop end_reading_instruction (
    .clk(Clock), .D(instruction_ready), .Q(l_PC), .reset(Reset));  // open: Qn, preset, en
  Adder #(.width(32)) adder_1 (.a(current_PC), .b(32'h4), .out(adder_1_out));  // open: cin, cout
  D_Flip_Flop d_ff_1 (.clk(Clock), .D(or_8_out), .Q(reset_IR), .reset(Reset));  // open: Qn, preset, en
  ram_manager ram_manager (
    .WT(Write_Time), .RT(Read_Time), .read_write(or_6_out), .start(or_7_out),
    .Address(multiplexer_2_out[19:2]), .RAM_OUTPUT0(RAM_Out_0), .RAM_OUPUT1(RAM_Out_1),
    .RAM_OUTPUT2(RAM_Out_2), .RAM_OUPUT3(RAM_Out_3), .RAM_INPUT0(RAM_WRITE), .ChipSelect(Chip_Select),
    .DataReady(end_ram_operation), .DataRead(RAM_OUT), .address_ram(Address), .Clock(Clock), .Reset(Reset),
    .r_w(nRead_Write), .ram_w0(RAM_In_0), .ram_w1(RAM_In_1), .ram_w2(RAM_In_2), .ram_w3(RAM_In_3),
    .ram_mask(Mask));
  Multiplexer #(.width(32), .enable("false")) multiplexer_4 (
    .in0(adder_1_out), .in1(A), .out(multiplexer_4_out), .sel(jr));
  or or_8 (or_8_out, Kbd_Enable, d_ff_9_q, or_18_out, or_9_out);
  Demultiplexer #(.select(3), .enable("false")) demultiplexer_3 (
    .out0(demultiplexer_3_out0), .out1(demultiplexer_3_out1), .out2(demultiplexer_3_out2),
    .out3(demultiplexer_3_out3), .out4(demultiplexer_3_out4), .out5(demultiplexer_3_out5),
    .out6(demultiplexer_3_out6), .out7(demultiplexer_3_out7), .in(l_PC), .sel(branch));
  Multiplexer #(.width(32), .enable("false")) multiplexer_5 (
    .in0(multiplexer_4_out), .in1({current_PC[31:28], direction, 2'b00}), .out(multiplexer_5_out), .sel(jmp));
  or or_9 (or_9_out, demultiplexer_3_out0, demultiplexer_3_out1, demultiplexer_3_out2, demultiplexer_3_out3);
  Adder #(.width(32)) adder_2 (.a(multiplexer_5_out), .b(K), .out(adder_2_out));  // open: cin, cout
  Demultiplexer #(.enable("false")) demultiplexer_4 (
    .out0(demultiplexer_4_out0), .out1(sp_enable0), .in(demultiplexer_3_out5), .sel(push));
  D_Flip_Flop d_ff_2 (.clk(Clock), .D(or_10_out), .Q(Stop), .reset(Reset));  // open: Qn, preset, en
  or or_10 (or_10_out, demultiplexer_3_out7, Stop);
  Multiplexer #(.width(32), .enable("false")) multiplexer_6 (
    .in0(multiplexer_5_out), .in1(adder_2_out), .out(multiplexer_6_out), .sel(or_11_out));
  or or_11 (or_11_out, bne_en, beq_en, blez_en, bltz_en, bgtz_en);
  D_Flip_Flop d_ff_3 (.clk(Clock), .D(demultiplexer_3_out4), .Q(start_RAM_op2), .reset(Reset));  // open: Qn, preset, en
  Register #(.width(32)) Program_Counter (.D(multiplexer_6_out), .en(l_PC), .Q(current_PC), .clk(Clock), .clr(Reset));
  or or_12 (or_12_out, demultiplexer_5_out0, start_RAM_op2);
  or or_13 (or_13_out, demultiplexer_4_out0, sp_enable0);
  D_Flip_Flop d_ff_4 (.clk(Clock), .D(or_12_out), .Q(d_ff_4_q), .reset(Reset));  // open: Qn, preset, en
  Demultiplexer #(.enable("false")) demultiplexer_5 (
    .out0(demultiplexer_5_out0), .out1(enable_RF1), .in(d_ff_4_q), .sel(end_ram_operation));
  D_Flip_Flop d_ff_5 (.clk(Clock), .D(or_13_out), .Q(RW1), .reset(Reset));  // open: Qn, preset, en
  Demultiplexer #(.enable("false")) demultiplexer_6 (
    .out0(demultiplexer_6_out0), .out1(enableHi_Lo), .in(d_ff_6_q), .sel(Hi_Lo_on));
  D_Flip_Flop d_ff_6 (.clk(Clock), .D(demultiplexer_3_out6), .Q(d_ff_6_q), .reset(Reset));  // open: Qn, preset, en
  instruction_decoder instruction_decoder_1 (
    .Instruction(IR), .in_2(Clock), .A_Selector(SA), .B_Selector(SB), .Write_Selector(SW), .ALU_op(ALU_OP),
    .Hi_Lo_operation(Hi_Lo_op), .Hi_Lo_enable(Hi_Lo_on), .Halt(is_halt), .dISel(dISel), .Branch(branch),
    .K(K), .Inmediate_Flag(IF), .tty(tty), .sw(sw_t), .Push(push), .Pop(pop), .load_word(lw), .jr(jr),
    .jmp(jmp), .direction(direction), .bne(bne), .beq(beq), .bgtz(bgtz), .blez(blez), .bltz(bltz));
  Demultiplexer #(.enable("false")) demultiplexer_7 (
    .out0(enable_RF0), .out1(TTY_Enable), .in(demultiplexer_6_out0), .sel(tty));
  or or_14 (or_14_out, demultiplexer_9_out0, RW1);
  D_Flip_Flop d_ff_7 (.clk(Clock), .D(enable_RF1), .Q(d_ff_7_q), .reset(Reset));  // open: Qn, preset, en
  Demultiplexer #(.enable("false")) demultiplexer_8 (
    .out0(demultiplexer_8_out0), .out1(sp_enable1), .in(d_ff_7_q), .sel(pop));
  D_Flip_Flop d_ff_8 (.clk(Clock), .D(or_14_out), .Q(d_ff_8_q), .reset(Reset));  // open: Qn, preset, en
  Demultiplexer #(.enable("false")) demultiplexer_9 (
    .out0(demultiplexer_9_out0), .out1(demultiplexer_9_out1), .in(d_ff_8_q), .sel(end_ram_operation));
  or or_15 (sp_enable, sp_enable0, sp_enable1);
  or or_16 (or_16_out, enable_RF0, TTY_Enable, enableHi_Lo);
  or or_17 (enable_RF, enable_RF1, enable_RF0);
  or or_18 (or_18_out, demultiplexer_8_out0, sp_enable1);
  D_Flip_Flop d_ff_9 (.clk(Clock), .D(demultiplexer_9_out1), .Q(d_ff_9_q), .reset(Reset));  // open: Qn, preset, en
  D_Flip_Flop d_ff_10 (.clk(Clock), .D(or_16_out), .Q(Kbd_Enable), .reset(Reset));  // open: Qn, preset, en
  assign bit_extender_1_out = {{25{1'b0}}, Kbd_ASCII_Data};  // Bit_Extender bit_extender_1
  Multiplexer #(.width(32), .enable("false")) multiplexer_7 (
    .in0({32{1'b1}}), .in1(bit_extender_1_out), .out(multiplexer_7_out), .sel(Kbd_Available));
  Random #(.width(32)) random_1 (.clk(Clock), .out(random_1_out));  // open: next, clr
  not not_4 (not_4_out, comparator_1_gt);
  Comparator #(.width(32)) comparator_1 (
    .a(A), .b({32{1'b0}}), .gt(comparator_1_gt), .lt(comparator_1_lt));  // open: eq
  Multiplexer #(.width(32), .enable("false")) multiplexer_8 (.in0(B), .in1(K), .out(multiplexer_8_out), .sel(IF));
  Multiplexer #(.select(3), .width(32), .enable("false")) multiplexer_9 (
    .in0(ALU_result), .in1(High), .in2(Low), .in3(multiplexer_7_out), .in4(random_1_out), .in5(RAM_OUT),
    .out(multiplexer_9_out), .sel(dISel));  // open: in6, in7
  Comparator #(.width(32)) comparator_2 (.a(B), .b(A), .eq(comparator_2_eq));  // open: gt, lt
  and and_2 (blez_en, blez, not_4_out);
  and and_3 (bltz_en, comparator_1_lt, bltz);
  alu alu_1 (.A(A), .B(multiplexer_8_out), .operation(ALU_OP), .Output(ALU_result));
  and and_4 (beq_en, comparator_2_eq, beq);
  and and_5 (bne_en, ~comparator_2_eq, bne);  // AND_Gate
  and and_6 (bgtz_en, bgtz, comparator_1_gt);
  registers registers_1 (
    .clk(Clock), .rst(Reset), .SA(SA), .SB(SB), .SW(SW), .data_input(multiplexer_9_out), .A(A), .B(B),
    .enable(enable_RF), .SP_en(sp_enable), .Push_Pop(push), .SP(SP));

  assign Kbd_Clear = Reset;

  // Other names for the same wires on the sheet: TTY_DATA[6:0] = TTY_ASCII_Data; CLK = Clock;
  //   CS_manager = Chip_Select; KBD_AVAIL = Kbd_Available; CLR = Reset; KBD_CLR = Reset;
  //   KBD_DATA[6:0] = Kbd_ASCII_Data; RAM_A[15:0] = Address; RAM_MASK[3:0] = Mask; RAM_OUTPUT_0[31:0] = RAM_Out_0;
  //   RAM_OUTPUT_1[31:0] = RAM_Out_1; RAM_OUTPUT_2[31:0] = RAM_Out_2; RAM_OUTPUT_3[31:0] = RAM_Out_3;
  //   rw0[31:0] = RAM_In_0; rw1_t[31:0] = RAM_In_1; rw2[31:0] = RAM_In_2; rw3[31:0] = RAM_In_3;
  //   RW_manager = nRead_Write; start_RAM_op1 = RW1

  // Notes on the sheet:
  //   RAM ADDRESS
  //   DATA FROM RAM
  //   DATA TO RAM
  //   DATA WRITE MASK
  //   RAM TIMING
  //   RAM CONTROL
  //   KEYBOARD
  //   TTY
  //   SEQUENCING
  //   Hi/Lo
  //   Instruction Decoder
  //   ALU
  //   RegisterFile
endmodule

module ram_manager (
  input  [3:0] WT,
  input  [3:0] RT,
  input  read_write,
  input  start,
  input  [17:0] Address,
  input  [31:0] RAM_OUTPUT0,
  input  [31:0] RAM_OUPUT1,
  input  [31:0] RAM_OUTPUT2,
  input  [31:0] RAM_OUPUT3,
  input  [31:0] RAM_INPUT0,
  input  Clock,
  input  Reset,
  output r_w,
  output ChipSelect,
  output DataReady,
  output [15:0] address_ram,
  output [31:0] DataRead,
  output [31:0] ram_w0,
  output [31:0] ram_w1,
  output [31:0] ram_w2,
  output [31:0] ram_w3,
  output [3:0] ram_mask
);

  wire and_1_out, cache_enable, cache_WRITE, \continue , CS1, d_ff_2_q, d_ff_3_q, d_ff_6_q, d_ff_8_q,
       d_ff_9_q, data_in_cache, demultiplexer_1_out0, demultiplexer_1_out1, demultiplexer_2_out1,
       demultiplexer_3_out0, demultiplexer_4_out0, demultiplexer_4_out1, IDLE_q, is_dirty, or_2_out,
       or_4_out, or_6_out, r, reset_dirty, reset_RL, staticRW, update_metadata, use_replace_line, useRL, w;
  wire [13:0] cache_tag;

  D_Flip_Flop d_ff_1 (.clk(Clock), .D(read_write), .Q(staticRW), .en(start), .reset(Reset));  // open: Qn, preset
  Multiplexer #(.width(14), .enable("false")) multiplexer_1 (
    .in0(Address[17:4]), .in1(cache_tag), .out(address_ram[15:2]), .sel(and_1_out));
  and and_1 (and_1_out, is_dirty, useRL);
  or or_1 (ChipSelect, CS1, r_w);
  or or_2 (or_2_out, DataReady, demultiplexer_1_out0);
  Demultiplexer #(.enable("false")) demultiplexer_1 (
    .out0(demultiplexer_1_out0), .out1(demultiplexer_1_out1), .in(IDLE_q), .sel(start));
  D_Flip_Flop IDLE (.clk(Clock), .D(or_2_out), .Q(IDLE_q), .preset(Reset));  // open: Qn, en, reset
  D_Flip_Flop d_ff_2 (.clk(Clock), .D(demultiplexer_1_out1), .Q(d_ff_2_q), .reset(Reset));  // open: Qn, preset, en
  or or_3 (reset_RL, or_6_out, d_ff_2_q);
  D_Flip_Flop d_ff_3 (.clk(Clock), .D(reset_RL), .Q(d_ff_3_q), .reset(Reset));  // open: Qn, preset, en
  D_Flip_Flop d_ff_4 (.clk(Clock), .D(1'b1), .Q(useRL), .en(use_replace_line), .reset(reset_RL));  // open: Qn, preset
  Demultiplexer #(.enable("false")) demultiplexer_2 (
    .out0(use_replace_line), .out1(demultiplexer_2_out1), .in(d_ff_3_q), .sel(data_in_cache));
  cache cache_1 (
    .Clock(Clock), .Reset(Reset), .cache_enable(cache_enable), .cache_write(cache_WRITE),
    .r_dirty(reset_dirty), .index(Address[3:2]), .offset(Address[1:0]), .tag(Address[17:4]),
    .RAM_INPUT(RAM_INPUT0), .RAM_OUTPUT0(RAM_OUTPUT0), .RAM_OUPUT1(RAM_OUPUT1), .RAM_OUTPUT2(RAM_OUTPUT2),
    .RAM_OUPUT3(RAM_OUPUT3), .data_in_cache(data_in_cache), .data_read(DataRead), .current_tag(cache_tag),
    .dirty(ram_mask), .DataWrite0(ram_w0), .DataWrite1(ram_w1), .DataWrite2(ram_w2), .DataWrite3(ram_w3),
    .useRL(useRL), .update_metadata(update_metadata));
  D_Flip_Flop d_ff_5 (.clk(Clock), .D(\continue ), .Q(reset_dirty), .reset(Reset));  // open: Qn, preset, en
  Demultiplexer #(.enable("false")) demultiplexer_3 (
    .out0(demultiplexer_3_out0), .out1(cache_WRITE), .in(demultiplexer_2_out1), .sel(staticRW));
  or or_4 (or_4_out, reset_dirty, demultiplexer_4_out0);
  Demultiplexer #(.enable("false")) demultiplexer_4 (
    .out0(demultiplexer_4_out0), .out1(demultiplexer_4_out1), .in(d_ff_6_q), .sel(is_dirty));
  D_Flip_Flop d_ff_6 (.clk(Clock), .D(use_replace_line), .Q(d_ff_6_q), .reset(Reset));  // open: Qn, preset, en
  or or_5 (update_metadata, demultiplexer_3_out0, cache_WRITE);
  \time  time_1 (
    .start(or_4_out), .r_w(1'b0), .reset(Reset), .\time (RT), .Clock(Clock), .r_w_2(r), .CS(CS1),
    .\end (cache_enable));
  D_Flip_Flop d_ff_7 (.clk(Clock), .D(update_metadata), .Q(DataReady), .reset(Reset));  // open: Qn, preset, en
  Comparator #(.width(4), .mode("unsigned")) comparator_1 (.a(ram_mask), .b(4'b0000), .gt(is_dirty));  // open: eq, lt
  \time  time_2 (
    .start(demultiplexer_4_out1), .r_w(1'b1), .reset(Reset), .\time (WT), .Clock(Clock), .r_w_2(w), .CS(r_w),
    .\end (\continue ));
  D_Flip_Flop d_ff_8 (.clk(Clock), .D(cache_enable), .Q(d_ff_8_q), .reset(Reset));  // open: Qn, preset, en
  D_Flip_Flop d_ff_9 (.clk(Clock), .D(d_ff_8_q), .Q(d_ff_9_q), .reset(Reset));  // open: Qn, preset, en
  buf or_6 (or_6_out, d_ff_9_q);  // OR_Gate

  assign address_ram[1:0] = Address[3:2];

  // Other names for the same wires on the sheet: offset[1:0] = Address[1:0]; tag[13:0] = Address[17:4];
  //   index[1:0] = Address[3:2]; CLK = Clock; CS0 = r_w; dirty[3:0] = ram_mask; end = DataReady;
  //   end_ram_op = DataReady; r_w_t = read_write; RAM_OUT[31:0] = DataRead; RAM_OUTPUT1[31:0] = RAM_OUPUT1;
  //   RAM_OUTPUT3[31:0] = RAM_OUPUT3; RST = Reset
endmodule

module RAM_Dispatcher (
  input  [3:0] WriteTime,
  input  Clock,
  input  CLR,
  output [31:0] Data,
  output [15:0] Address,
  output [3:0] Mask,
  output Finished,
  output Write
);

  wire demultiplexer_2_out1, demultiplexer_3_out1, End, IDLE_q, IncAddr, Load, or_1_out, or_2_out, While_q,
       WriteEnd;
  wire [3:0] counter_1_q;
  wire [31:0] CurrentAddress_q;

  Counter #(.width(32), .max('hffffffff)) CurrentAddress (
    .count(IncAddr), .Q({CurrentAddress_q[31:18], Address, CurrentAddress_q[1:0]}), .clk(Clock), .clr(CLR));  // open: load, D, carry
  or or_1 (or_1_out, IncAddr, demultiplexer_3_out1, Finished);
  D_Flip_Flop IDLE (.clk(Clock), .D(or_1_out), .Q(IDLE_q), .preset(CLR));  // open: Qn, en, reset
  Demultiplexer #(.enable("false")) demultiplexer_1 (.out0(Load), .out1(Finished), .in(IDLE_q), .sel(End));
  D_Flip_Flop While (.clk(Clock), .D(or_2_out), .Q(While_q), .reset(CLR));  // open: Qn, preset, en
  or or_2 (or_2_out, Write, Load);
  RAM_part #(.addrWidth(18), .dataWidth(32)) ram_1 (
    .addr({Address, CurrentAddress_q[1:0]}), .data(Data), .clk(Clock));  // open: sel, ld, clr
  Demultiplexer #(.enable("false")) demultiplexer_2 (
    .out0(Write), .out1(demultiplexer_2_out1), .in(While_q), .sel(WriteEnd));
  Decoder #(.select(2)) decoder_1 (
    .out0(Mask[0]), .out1(Mask[1]), .out2(Mask[2]), .out3(Mask[3]), .sel(CurrentAddress_q[1:0]));  // open: en
  Demultiplexer #(.enable("false")) demultiplexer_3 (
    .out0(IncAddr), .out1(demultiplexer_3_out1), .in(demultiplexer_2_out1), .sel(End));
  Counter #(.width(4), .max('hf)) counter_1 (
    .load(Load), .D(WriteTime), .count(Write), .Q(counter_1_q), .clk(Clock));  // open: carry, clr
  Comparator #(.width(32)) comparator_1 (.a(Data), .b({32{1'b1}}), .eq(End));  // open: gt, lt
  Comparator #(.width(4)) comparator_2 (.a(4'b0000), .b(counter_1_q), .eq(WriteEnd));  // open: gt, lt

  // Other names for the same wires on the sheet: CLK = Clock; Count = Write; WT[3:0] = WriteTime
endmodule

module registers (
  input  [4:0] SA,
  input  [4:0] SB,
  input  [4:0] SW,
  input  [31:0] data_input,
  input  clk,
  input  rst,
  input  enable,
  input  SP_en,
  input  Push_Pop,
  output [31:0] A,
  output [31:0] B,
  output [31:0] SP
);

  wire enableR0, enableR1, enableR2, enableR3, enableR4, enableR5, enableR6, enableR7, enableR8, enableR9,
       enableR10, enableR11, enableR12, enableR13, enableR14, enableR15, enableR16, enableR17, enableR18,
       enableR19, enableR20, enableR21, enableR22, enableR23, enableR24, enableR25, enableR26, enableR27,
       enableR28, enableR29, enableR30, enableR31, or_1_out;
  wire [31:0] multiplexer_3_out, multiplexer_4_out, r0out, r1out, r2out, r3out, r4out, r5out, r6out, r7out,
       r8out, r9out, r10out, r11out, r12out, r13out, r14out, r15out, r16out, r17out, r18out, r19out, r20out,
       r21out, r22out, r23out, r24out, r25out, r26out, r27out, r28out, r29out, r30out, SP_4, SP_4_t;

  Register #(.width(32)) R0 (.D({32{1'b0}}), .en(enableR0), .Q(r0out), .clk(clk), .clr(rst));
  Register #(.width(32)) R8 (.D(data_input), .en(enableR8), .Q(r8out), .clk(clk), .clr(rst));
  Register #(.width(32)) R16 (.D(data_input), .en(enableR16), .Q(r16out), .clk(clk), .clr(rst));
  Register #(.width(32)) R24 (.D(data_input), .en(enableR24), .Q(r24out), .clk(clk), .clr(rst));
  Register #(.width(32)) R1 (.D(data_input), .en(enableR1), .Q(r1out), .clk(clk), .clr(rst));
  Register #(.width(32)) R9 (.D(data_input), .en(enableR9), .Q(r9out), .clk(clk), .clr(rst));
  Register #(.width(32)) R17 (.D(data_input), .en(enableR17), .Q(r17out), .clk(clk), .clr(rst));
  Register #(.width(32)) R25 (.D(data_input), .en(enableR25), .Q(r25out), .clk(clk), .clr(rst));
  Multiplexer #(.select(5), .width(32), .enable("false")) multiplexer_1 (
    .in0(r0out), .in1(r1out), .in2(r2out), .in3(r3out), .in4(r4out), .in5(r5out), .in6(r6out), .in7(r7out),
    .in8(r8out), .in9(r9out), .in10(r10out), .in11(r11out), .in12(r12out), .in13(r13out), .in14(r14out),
    .in15(r15out), .in16(r16out), .in17(r17out), .in18(r18out), .in19(r19out), .in20(r20out), .in21(r21out),
    .in22(r22out), .in23(r23out), .in24(r24out), .in25(r25out), .in26(r26out), .in27(r27out), .in28(r28out),
    .in29(r29out), .in30(r30out), .in31(SP), .out(A), .sel(SA));
  Register #(.width(32)) R2 (.D(data_input), .en(enableR2), .Q(r2out), .clk(clk), .clr(rst));
  Register #(.width(32)) R10 (.D(data_input), .en(enableR10), .Q(r10out), .clk(clk), .clr(rst));
  Register #(.width(32)) R18 (.D(data_input), .en(enableR18), .Q(r18out), .clk(clk), .clr(rst));
  Register #(.width(32)) R26 (.D(data_input), .en(enableR26), .Q(r26out), .clk(clk), .clr(rst));
  Register #(.width(32)) R3 (.D(data_input), .en(enableR3), .Q(r3out), .clk(clk), .clr(rst));
  Register #(.width(32)) R11 (.D(data_input), .en(enableR11), .Q(r11out), .clk(clk), .clr(rst));
  Register #(.width(32)) R19 (.D(data_input), .en(enableR19), .Q(r19out), .clk(clk), .clr(rst));
  Register #(.width(32)) R27 (.D(data_input), .en(enableR27), .Q(r27out), .clk(clk), .clr(rst));
  Register #(.width(32)) R4 (.D(data_input), .en(enableR4), .Q(r4out), .clk(clk), .clr(rst));
  Register #(.width(32)) R12 (.D(data_input), .en(enableR12), .Q(r12out), .clk(clk), .clr(rst));
  Register #(.width(32)) R20 (.D(data_input), .en(enableR20), .Q(r20out), .clk(clk), .clr(rst));
  Register #(.width(32)) R28 (.D(data_input), .en(enableR28), .Q(r28out), .clk(clk), .clr(rst));
  Multiplexer #(.select(5), .width(32), .enable("false")) multiplexer_2 (
    .in0(r0out), .in1(r1out), .in2(r2out), .in3(r3out), .in4(r4out), .in5(r5out), .in6(r6out), .in7(r7out),
    .in8(r8out), .in9(r9out), .in10(r10out), .in11(r11out), .in12(r12out), .in13(r13out), .in14(r14out),
    .in15(r15out), .in16(r16out), .in17(r17out), .in18(r18out), .in19(r19out), .in20(r20out), .in21(r21out),
    .in22(r22out), .in23(r23out), .in24(r24out), .in25(r25out), .in26(r26out), .in27(r27out), .in28(r28out),
    .in29(r29out), .in30(r30out), .in31(SP), .out(B), .sel(SB));
  Register #(.width(32)) R5 (.D(data_input), .en(enableR5), .Q(r5out), .clk(clk), .clr(rst));
  Register #(.width(32)) R13 (.D(data_input), .en(enableR13), .Q(r13out), .clk(clk), .clr(rst));
  Register #(.width(32)) R21 (.D(data_input), .en(enableR21), .Q(r21out), .clk(clk), .clr(rst));
  Register #(.width(32)) R29 (.D(data_input), .en(enableR29), .Q(r29out), .clk(clk), .clr(rst));
  Register #(.width(32)) R6 (.D(data_input), .en(enableR6), .Q(r6out), .clk(clk), .clr(rst));
  Register #(.width(32)) R14 (.D(data_input), .en(enableR14), .Q(r14out), .clk(clk), .clr(rst));
  Register #(.width(32)) R22 (.D(data_input), .en(enableR22), .Q(r22out), .clk(clk), .clr(rst));
  Register #(.width(32)) R30 (.D(data_input), .en(enableR30), .Q(r30out), .clk(clk), .clr(rst));
  Register #(.width(32)) R7 (.D(data_input), .en(enableR7), .Q(r7out), .clk(clk), .clr(rst));
  Register #(.width(32)) R15 (.D(data_input), .en(enableR15), .Q(r15out), .clk(clk), .clr(rst));
  Register #(.width(32)) R23 (.D(data_input), .en(enableR23), .Q(r23out), .clk(clk), .clr(rst));
  Multiplexer #(.width(32), .enable("false")) multiplexer_3 (
    .in0(SP_4), .in1(SP_4_t), .out(multiplexer_3_out), .sel(Push_Pop));
  Multiplexer #(.width(32), .enable("false")) multiplexer_4 (
    .in0(data_input), .in1(multiplexer_3_out), .out(multiplexer_4_out), .sel(SP_en));
  Demultiplexer #(.select(5), .enable("false")) demultiplexer_1 (
    .out0(enableR0), .out1(enableR1), .out2(enableR2), .out3(enableR3), .out4(enableR4), .out5(enableR5),
    .out6(enableR6), .out7(enableR7), .out8(enableR8), .out9(enableR9), .out10(enableR10), .out11(enableR11),
    .out12(enableR12), .out13(enableR13), .out14(enableR14), .out15(enableR15), .out16(enableR16),
    .out17(enableR17), .out18(enableR18), .out19(enableR19), .out20(enableR20), .out21(enableR21),
    .out22(enableR22), .out23(enableR23), .out24(enableR24), .out25(enableR25), .out26(enableR26),
    .out27(enableR27), .out28(enableR28), .out29(enableR29), .out30(enableR30), .out31(enableR31),
    .in(enable), .sel(SW));
  or or_1 (or_1_out, enableR31, SP_en);
  Adder #(.width(32)) adder_1 (.a(32'h4), .b(SP), .out(SP_4));  // open: cin, cout
  Subtractor #(.width(32)) subtractor_1 (.a(SP), .b(32'h4), .out(SP_4_t));  // open: bin, bout
  Register #(.width(32)) R31_SP (.D(multiplexer_4_out), .en(or_1_out), .Q(SP), .clk(clk), .clr(rst));

  // Other names for the same wires on the sheet: A_out[31:0] = A; B_out[31:0] = B; enable_stack_pointer = SP_en;
  //   SP_out[31:0] = SP
endmodule

module hi_lo (
  input  [31:0] A,
  input  [31:0] B,
  input  clk,
  input  rst,
  input  [1:0] op_selector,
  input  enable,
  output [31:0] Low,
  output [31:0] High
);

  wire adder_2_cout, adder_4_cout, xor_1_out;
  wire [15:0] mix1_high, mix1_low, mix2_high, mix2_low;
  wire [31:0] adder_1_out, adder_2_out, adder_3_out, bit_extender_5_out, bit_extender_6_out, Div, divHigh,
       divLow, divuHigh, divuLow, mulHigh, mulLow, multiplexer_1_out, multiplexer_4_out, multiplexer_7_out,
       muluHigh, muluLow, negator_1_out, negator_2_out, negator_3_out, prehigh, prelower, Rem,
       subtractor_1_out, value_1_0, value_1_1, value_2_0, value_2_1, X1, Y1;

  Negator #(.width(32)) negator_1 (.in(A), .out(negator_1_out));
  Negator #(.width(32)) negator_2 (.in(B), .out(negator_2_out));
  Multiplexer #(.select(2), .width(32), .enable("false")) multiplexer_1 (
    .in0(mulHigh), .in1(muluHigh), .in2(divHigh), .in3(divuHigh), .out(multiplexer_1_out), .sel(op_selector));
  Multiplier #(.width(32)) multiplier_1 (.a(A), .b(B), .out(mulLow), .cout(mulHigh));  // open: cin
  Multiplexer #(.width(32), .enable("false")) multiplexer_2 (.in0(A), .in1(negator_1_out), .out(X1), .sel(A[31]));
  Multiplexer #(.width(32), .enable("false")) multiplexer_3 (.in0(B), .in1(negator_2_out), .out(Y1), .sel(B[31]));
  Register #(.width(32)) u_High (.D(multiplexer_1_out), .en(enable), .Q(High), .clk(clk), .clr(rst));
  Divider #(.width(32)) divider_1 (.a(X1), .b(Y1), .out(Div), .rem(Rem));  // open: upper
  Adder #(.width(32)) adder_1 (.a(Div), .b(32'h1), .out(adder_1_out));  // open: cin, cout
  Divider #(.width(32)) divider_2 (.a(A), .b(B), .out(divuLow), .rem(divuHigh));  // open: upper
  Multiplexer #(.width(32), .enable("false")) multiplexer_4 (
    .in0(Div), .in1(adder_1_out), .out(multiplexer_4_out), .sel(A[31]));
  Multiplexer #(.width(32), .enable("false")) multiplexer_5 (
    .in0(multiplexer_4_out), .in1(negator_3_out), .out(divLow), .sel(xor_1_out));
  Negator #(.width(32)) negator_3 (.in(multiplexer_4_out), .out(negator_3_out));
  xor xor_1 (xor_1_out, B[31], A[31]);
  Subtractor #(.width(32)) subtractor_1 (.a(Y1), .b(Rem), .out(subtractor_1_out));  // open: bin, bout
  Multiplexer #(.width(32), .enable("false")) multiplexer_6 (
    .in0(Rem), .in1(subtractor_1_out), .out(divHigh), .sel(A[31]));
  Multiplexer #(.select(2), .width(32), .enable("false")) multiplexer_7 (
    .in0(mulLow), .in1(muluLow), .in2(divLow), .in3(divuLow), .out(multiplexer_7_out), .sel(op_selector));
  Register #(.width(32)) u_Low (.D(multiplexer_7_out), .en(enable), .Q(Low), .clk(clk), .clr(rst));
  assign value_1_0 = {{16{1'b0}}, A[15:0]};  // Bit_Extender bit_extender_1
  assign value_1_1 = {{16{1'b0}}, A[31:16]};  // Bit_Extender bit_extender_2
  assign value_2_0 = {{16{1'b0}}, B[15:0]};  // Bit_Extender bit_extender_3
  assign value_2_1 = {{16{1'b0}}, B[31:16]};  // Bit_Extender bit_extender_4
  Multiplier #(.width(32)) multiplier_2 (.a(value_1_0), .b(value_2_0), .out(prelower));  // open: cin, cout
  Multiplier #(.width(32)) multiplier_3 (.a(value_1_0), .b(value_2_1), .out({mix1_high, mix1_low}));  // open: cin, cout
  Multiplier #(.width(32)) multiplier_4 (.a(value_1_1), .b(value_2_0), .out({mix2_high, mix2_low}));  // open: cin, cout
  Multiplier #(.width(32)) multiplier_5 (.a(value_1_1), .b(value_2_1), .out(prehigh));  // open: cin, cout
  assign bit_extender_5_out = {{16{1'b0}}, mix1_high};  // Bit_Extender bit_extender_5
  assign bit_extender_6_out = {{16{1'b0}}, mix2_high};  // Bit_Extender bit_extender_6
  Adder #(.width(32)) adder_2 (
    .a({mix1_low, {16{1'b0}}}), .b({mix2_low, {16{1'b0}}}), .out(adder_2_out), .cout(adder_2_cout));  // open: cin
  Adder #(.width(32)) adder_3 (
    .a(bit_extender_5_out), .b(bit_extender_6_out), .out(adder_3_out), .cin(adder_2_cout));  // open: cout
  Adder #(.width(32)) adder_4 (.a(prelower), .b(adder_2_out), .out(muluLow), .cout(adder_4_cout));  // open: cin
  Adder #(.width(32)) adder_5 (.a(prehigh), .b(adder_3_out), .out(muluHigh), .cin(adder_4_cout));  // open: cout

  // Other names for the same wires on the sheet: SignX = A[31]; SignY = B[31]
endmodule

module alu (
  input  [31:0] A,
  input  [31:0] B,
  input  [2:0] operation,
  output [31:0] Output
);

  wire comparator_1_lt, comparator_2_lt;
  wire [31:0] add, \and , \nor , \or , slt, sltu, sub, \xor ;

  Adder #(.width(32)) adder_1 (.a(A), .b(B), .out(add));  // open: cin, cout
  Subtractor #(.width(32)) subtractor_1 (.a(A), .b(B), .out(sub));  // open: bin, bout
  Comparator #(.width(32)) comparator_1 (.a(A), .b(B), .lt(comparator_1_lt));  // open: gt, eq
  Comparator #(.width(32), .mode("unsigned")) comparator_2 (.a(A), .b(B), .lt(comparator_2_lt));  // open: gt, eq
  assign slt = {{31{1'b0}}, comparator_1_lt};  // Bit_Extender bit_extender_1
  assign sltu = {{31{1'b0}}, comparator_2_lt};  // Bit_Extender bit_extender_2
  assign \and  = A & B;  // AND_Gate and_1, 32 bits wide
  assign \or  = A | B;  // OR_Gate or_1, 32 bits wide
  assign \nor  = ~(A | B);  // NOR_Gate nor_1, 32 bits wide
  assign \xor  = A ^ B;  // XOR_Gate xor_1, 32 bits wide
  Multiplexer #(.select(3), .width(32), .enable("false")) multiplexer_1 (
    .in0(add), .in1(sub), .in2(slt), .in3(sltu), .in4(\and ), .in5(\nor ), .in6(\xor ), .in7(\or ),
    .out(Output), .sel(operation));
endmodule

module instruction_decoder (
  input  [31:0] Instruction,
  input  in_2,
  output [4:0] A_Selector,
  output [4:0] B_Selector,
  output [4:0] Write_Selector,
  output [2:0] ALU_op,
  output [1:0] Hi_Lo_operation,
  output Hi_Lo_enable,
  output Halt,
  output [2:0] dISel,
  output [2:0] Branch,
  output [31:0] K,
  output Inmediate_Flag,
  output tty,
  output sw,
  output Push,
  output Pop,
  output load_word,
  output jr,
  output jmp,
  output [25:0] direction,
  output bne,
  output beq,
  output bgtz,
  output blez,
  output bltz
);

  wire _000_000, _111_000, _111_111, add, addi, \and , andi, Arithmetic, BF, div, divu, k_En, kbd, mfhi,
       mflo, mult, mulu, \nor , not_recognized, \or , or_1_out, or_2_out, or_3_out, or_4_out, or_5_out,
       or_6_out, or_7_out, or_8_out, or_9_out, or_10_out, or_12_out, or_13_out, or_14_out, or_15_out,
       or_16_out, or_17_out, or_18_out, or_20_out, ori, rnd, slt, slti, sltiu, sltu, sub, \xor , xori;
  wire [1:0] k_selector;
  wire [5:0] func_code;
  wire [29:0] bit_extender_1_out;
  wire [31:0] bit_extender_2_out, bit_extender_3_out;

  or or_1 (or_1_out, \or , ori);
  Comparator #(.width(6), .mode("unsigned")) comparator_1 (
    .a(Instruction[31:26]), .b({6{1'b0}}), .eq(_000_000));  // open: gt, lt
  Comparator #(.width(6), .mode("unsigned")) comparator_2 (
    .a(Instruction[31:26]), .b(6'b111000), .eq(_111_000));  // open: gt, lt
  Comparator #(.width(6), .mode("unsigned")) comparator_3 (
    .a(Instruction[31:26]), .b({6{1'b1}}), .eq(_111_111));  // open: gt, lt
  or or_2 (or_2_out, \xor , xori);
  or or_3 (or_3_out, \and , andi);
  or or_4 (or_4_out, Push, sw);
  or or_5 (or_5_out, rnd, tty, or_6_out, Arithmetic);
  or or_6 (or_6_out, kbd, mflo, mfhi);
  or or_7 (or_7_out, sltu, sltiu);
  or or_8 (or_8_out, Pop, load_word);
  or or_9 (or_9_out, slti, slt);
  nor nor_1 (not_recognized, Halt, or_5_out, or_4_out, or_8_out);
  or or_10 (or_10_out, add, addi);
  or or_11 (Arithmetic, or_10_out, sub, or_9_out, or_7_out, or_3_out, \nor , or_2_out, or_1_out, Hi_Lo_enable);
  Priority_Encoder priority_encoder_1 (
    .in0(not_recognized), .in1(not_recognized), .in2(not_recognized), .in3(not_recognized), .in4(or_8_out),
    .in5(or_4_out), .in6(or_5_out), .in7(Halt), .out(Branch));  // open: en_in, gs, en_out
  or or_12 (or_12_out, load_word, Pop);
  or or_13 (or_13_out, sw, load_word, or_10_out);
  assign func_code = or_18_out ? Instruction[5:0] : 6'bz;  // Controlled_Buffer controlled_buffer_1
  assign Write_Selector = or_18_out ? Instruction[15:11] : 5'bz;  // Controlled_Buffer controlled_buffer_2
  assign func_code = _111_111 ? Instruction[5:0] : 6'bz;  // Controlled_Buffer controlled_buffer_3
  assign Write_Selector = or_15_out ? Instruction[15:11] : 5'bz;  // Controlled_Buffer controlled_buffer_4
  assign A_Selector = tty ? Instruction[25:21] : 5'bz;  // Controlled_Buffer controlled_buffer_5
  Priority_Encoder priority_encoder_2 (
    .in0(Arithmetic), .in1(mfhi), .in2(mflo), .in3(kbd), .in4(rnd), .in5(or_12_out), .out(dISel));  // open: in6, in7, en_in, gs, en_out
  Priority_Encoder priority_encoder_3 (
    .in0(or_13_out), .in1(sub), .in2(or_9_out), .in3(or_7_out), .in4(or_3_out), .in5(\nor ), .in6(or_2_out),
    .in7(or_1_out), .out(ALU_op));  // open: en_in, gs, en_out
  or or_14 (or_14_out, slti, addi, sltiu, andi, ori, xori, load_word);
  assign A_Selector = or_14_out ? Instruction[25:21] : 5'bz;  // Controlled_Buffer controlled_buffer_6
  assign Write_Selector = or_14_out ? Instruction[20:16] : 5'bz;  // Controlled_Buffer controlled_buffer_7
  assign B_Selector = or_18_out ? Instruction[20:16] : 5'bz;  // Controlled_Buffer controlled_buffer_8
  assign A_Selector = or_18_out ? Instruction[25:21] : 5'bz;  // Controlled_Buffer controlled_buffer_9
  or or_15 (or_15_out, kbd, rnd);
  or or_16 (or_16_out, sltiu, slti, load_word, addi, sw);
  or or_17 (or_17_out, xori, andi, ori);
  or or_18 (or_18_out, _000_000, _111_000);
  or or_19 (Inmediate_Flag, or_16_out, or_17_out);
  or or_20 (or_20_out, sw, BF);
  assign bit_extender_1_out = {{14{Instruction[15]}}, Instruction[15:0]};  // Bit_Extender bit_extender_1
  assign bit_extender_2_out = {{16{Instruction[15]}}, Instruction[15:0]};  // Bit_Extender bit_extender_2
  assign bit_extender_3_out = {{16{1'b0}}, Instruction[15:0]};  // Bit_Extender bit_extender_3
  Priority_Encoder #(.select(2)) priority_encoder_4 (
    .in0(BF), .in1(or_16_out), .in2(or_17_out), .out(k_selector), .gs(k_En));  // open: in3, en_out, en_in
  or or_21 (Hi_Lo_enable, mult, mulu, div, divu);
  Priority_Encoder #(.select(2)) priority_encoder_5 (
    .in0(mult), .in1(mulu), .in2(div), .in3(divu), .out(Hi_Lo_operation));  // open: gs, en_out, en_in
  assign B_Selector = or_20_out ? Instruction[20:16] : 5'bz;  // Controlled_Buffer controlled_buffer_10
  assign A_Selector = or_20_out ? Instruction[25:21] : 5'bz;  // Controlled_Buffer controlled_buffer_11
  or or_22 (BF, bne, beq, bgtz, blez, bltz);
  assign Write_Selector = or_20_out ? {5{1'b0}} : 5'bz;  // Controlled_Buffer controlled_buffer_12
  Multiplexer #(.select(2), .width(32)) multiplexer_1 (
    .in0({bit_extender_1_out, 2'b00}), .in1(bit_extender_2_out), .in2(bit_extender_3_out), .out(K),
    .sel(k_selector), .en(k_En));  // open: in3
  and and_1 (Pop, _111_000, ~func_code[5], ~func_code[4], ~func_code[3], ~func_code[2], ~func_code[1], ~func_code[0]);  // AND_Gate
  and and_2 (mfhi, _000_000, ~func_code[5], func_code[4], ~func_code[3], ~func_code[2], ~func_code[1], ~func_code[0]);  // AND_Gate
  and and_3 (add, _000_000, func_code[5], ~func_code[4], ~func_code[3], ~func_code[2], ~func_code[1], ~func_code[0]);  // AND_Gate
  and and_4 (slt, _000_000, func_code[5], ~func_code[4], func_code[3], ~func_code[2], func_code[1], ~func_code[0]);  // AND_Gate
  and and_5 (jr, _000_000, ~func_code[5], ~func_code[4], func_code[3], ~func_code[2], ~func_code[1], ~func_code[0]);  // AND_Gate
  and and_6 (addi, ~Instruction[31], ~Instruction[30], Instruction[29], ~Instruction[28], ~Instruction[27], ~Instruction[26]);  // AND_Gate
  and and_7 (andi, ~Instruction[31], ~Instruction[30], Instruction[29], Instruction[28], ~Instruction[27], ~Instruction[26]);  // AND_Gate
  and and_8 (xori, ~Instruction[31], ~Instruction[30], Instruction[29], Instruction[28], Instruction[27], ~Instruction[26]);  // AND_Gate
  and and_9 (rnd, _111_111, ~func_code[5], ~func_code[4], ~func_code[3], ~func_code[2], func_code[1], ~func_code[0]);  // AND_Gate
  and and_10 (bgtz, ~Instruction[31], ~Instruction[30], ~Instruction[29], Instruction[28], Instruction[27], Instruction[26]);  // AND_Gate
  and and_11 (blez, ~Instruction[31], ~Instruction[30], ~Instruction[29], Instruction[28], Instruction[27], ~Instruction[26]);  // AND_Gate
  and and_12 (bltz, ~Instruction[31], ~Instruction[30], ~Instruction[29], ~Instruction[28], ~Instruction[27], Instruction[26]);  // AND_Gate
  and and_13 (slti, ~Instruction[31], ~Instruction[30], Instruction[29], ~Instruction[28], Instruction[27], ~Instruction[26]);  // AND_Gate
  and and_14 (sltiu, ~Instruction[31], ~Instruction[30], Instruction[29], ~Instruction[28], Instruction[27], Instruction[26]);  // AND_Gate
  and and_15 (ori, ~Instruction[31], ~Instruction[30], Instruction[29], Instruction[28], ~Instruction[27], Instruction[26]);  // AND_Gate
  and and_16 (tty, _111_111, ~func_code[5], ~func_code[4], ~func_code[3], ~func_code[2], ~func_code[1], func_code[0]);  // AND_Gate
  and and_17 (load_word, Instruction[31], ~Instruction[30], ~Instruction[29], ~Instruction[28], Instruction[27], Instruction[26]);  // AND_Gate
  and and_18 (mflo, _000_000, ~func_code[5], func_code[4], ~func_code[3], ~func_code[2], func_code[1], ~func_code[0]);  // AND_Gate
  and and_19 (sub, _000_000, func_code[5], ~func_code[4], ~func_code[3], ~func_code[2], func_code[1], ~func_code[0]);  // AND_Gate
  and and_20 (sltu, _000_000, func_code[5], ~func_code[4], func_code[3], ~func_code[2], func_code[1], func_code[0]);  // AND_Gate
  and and_21 (\xor , _000_000, func_code[5], ~func_code[4], func_code[3], ~func_code[2], ~func_code[1], ~func_code[0]);  // AND_Gate
  and and_22 (\and , _000_000, func_code[5], ~func_code[4], ~func_code[3], func_code[2], ~func_code[1], ~func_code[0]);  // AND_Gate
  and and_23 (mult, _000_000, ~func_code[5], func_code[4], func_code[3], ~func_code[2], ~func_code[1], ~func_code[0]);  // AND_Gate
  and and_24 (div, _000_000, ~func_code[5], func_code[4], func_code[3], ~func_code[2], func_code[1], ~func_code[0]);  // AND_Gate
  and and_25 (bne, ~Instruction[31], ~Instruction[30], ~Instruction[29], Instruction[28], ~Instruction[27], Instruction[26]);  // AND_Gate
  and and_26 (beq, ~Instruction[31], ~Instruction[30], ~Instruction[29], Instruction[28], ~Instruction[27], ~Instruction[26]);  // AND_Gate
  and and_27 (\or , _000_000, func_code[5], ~func_code[4], ~func_code[3], func_code[2], ~func_code[1], func_code[0]);  // AND_Gate
  and and_28 (\nor , _000_000, func_code[5], ~func_code[4], ~func_code[3], func_code[2], func_code[1], func_code[0]);  // AND_Gate
  and and_29 (mulu, _000_000, ~func_code[5], func_code[4], func_code[3], ~func_code[2], ~func_code[1], func_code[0]);  // AND_Gate
  and and_30 (Push, _111_000, ~func_code[5], ~func_code[4], ~func_code[3], ~func_code[2], ~func_code[1], func_code[0]);  // AND_Gate
  and and_31 (divu, _000_000, ~func_code[5], func_code[4], func_code[3], ~func_code[2], func_code[1], func_code[0]);  // AND_Gate
  and and_32 (Halt, _111_111, func_code[5], func_code[4], func_code[3], func_code[2], func_code[1], func_code[0]);
  and and_33 (kbd, _111_111, ~func_code[5], ~func_code[4], ~func_code[3], func_code[2], ~func_code[1], ~func_code[0]);  // AND_Gate
  and and_34 (sw, Instruction[31], ~Instruction[30], Instruction[29], ~Instruction[28], Instruction[27], Instruction[26]);  // AND_Gate
  and and_35 (jmp, ~Instruction[31], ~Instruction[30], ~Instruction[29], ~Instruction[28], Instruction[27], ~Instruction[26]);  // AND_Gate

  assign direction = Instruction[25:0];

  // Other names for the same wires on the sheet: clk = in_2; instruction_t[25:0] = Instruction[25:0];
  //   k_t[15:0] = Instruction[15:0]; Hi_Lo_op[1:0] = Hi_Lo_operation; IF = Inmediate_Flag;
  //   op_code[5:0] = Instruction[31:26]; SA[4:0] = A_Selector; SB[4:0] = B_Selector; store_word = sw;
  //   SW_t[4:0] = Write_Selector
endmodule

module \time  (
  input  start,
  input  r_w,
  input  reset,
  input  [3:0] \time ,
  input  Clock,
  output r_w_2,
  output \end ,
  output CS
);

  wire cs0, d_ff_1_q, d_ff_2_q, d_ff_3_q, demultiplexer_1_out0, demultiplexer_1_out1, demultiplexer_2_out0,
       OP_READY, or_1_out, reset_counter;
  wire [3:0] counter_1_q;

  Counter #(.width(4), .max('hf)) counter_1 (
    .count(cs0), .Q(counter_1_q), .clk(Clock), .clr(or_1_out));  // open: load, D, carry
  or or_1 (or_1_out, reset, reset_counter);
  or or_2 (reset_counter, d_ff_3_q, demultiplexer_1_out0);
  Demultiplexer #(.enable("false")) demultiplexer_1 (
    .out0(demultiplexer_1_out0), .out1(demultiplexer_1_out1), .in(d_ff_1_q), .sel(start));
  D_Flip_Flop d_ff_1 (.clk(Clock), .D(reset_counter), .Q(d_ff_1_q), .preset(reset));  // open: Qn, en, reset
  or or_3 (cs0, demultiplexer_2_out0, demultiplexer_1_out1);
  or or_4 (CS, \end , cs0);
  Comparator #(.width(4), .mode("unsigned")) comparator_1 (.a(counter_1_q), .b(\time ), .eq(OP_READY));  // open: gt, lt
  Demultiplexer #(.enable("false")) demultiplexer_2 (
    .out0(demultiplexer_2_out0), .out1(\end ), .in(d_ff_2_q), .sel(OP_READY));
  D_Flip_Flop d_ff_2 (.clk(Clock), .D(cs0), .Q(d_ff_2_q), .reset(reset));  // open: Qn, preset, en
  D_Flip_Flop d_ff_3 (.clk(Clock), .D(\end ), .Q(d_ff_3_q), .reset(reset));  // open: Qn, preset, en

  assign r_w_2 = r_w;

  // Other names for the same wires on the sheet: CLK = Clock; cs1 = \end ; enable_counter = cs0
endmodule

module cache (
  input  Clock,
  input  Reset,
  input  cache_enable,
  input  cache_write,
  input  r_dirty,
  input  [1:0] index,
  input  [1:0] offset,
  input  [13:0] tag,
  input  [31:0] RAM_INPUT,
  input  [31:0] RAM_OUTPUT0,
  input  [31:0] RAM_OUPUT1,
  input  [31:0] RAM_OUTPUT2,
  input  [31:0] RAM_OUPUT3,
  input  useRL,
  input  update_metadata,
  output data_in_cache,
  output [31:0] data_read,
  output [13:0] current_tag,
  output [3:0] dirty,
  output [31:0] DataWrite0,
  output [31:0] DataWrite1,
  output [31:0] DataWrite2,
  output [31:0] DataWrite3
);

  wire _0, _1, _2, _3, and_1_out, and_2_out, and_3_out, and_4_out, and_5_out, and_6_out, and_7_out,
       and_8_out, and_9_out, and_10_out, and_11_out, and_12_out, and_13_out, and_14_out, and_15_out,
       and_16_out, data_in_cache0, data_in_cache1, data_in_cache2, data_in_cache3;
  wire [3:0] dirty0, dirty1, dirty2, dirty3;
  wire [13:0] current_tag0, current_tag1, current_tag2, current_tag3;
  wire [31:0] data_read0, data_read1, data_read2, data_read3, dw00, dw01, dw02, dw03, dw10, dw11, dw12, dw13,
       dw20, dw21, dw22, dw23, dw30, dw31, dw32, dw33;

  and and_1 (and_1_out, r_dirty, _3);
  and and_2 (and_2_out, r_dirty, _0);
  and and_3 (and_3_out, update_metadata, _0);
  and and_4 (and_4_out, r_dirty, _1);
  and and_5 (and_5_out, update_metadata, _1);
  and and_6 (and_6_out, r_dirty, _2);
  and and_7 (and_7_out, update_metadata, _2);
  and and_8 (and_8_out, update_metadata, _3);
  block_cache block_cache_1 (
    .Clock(Clock), .Reset(Reset), .cache_enable(and_12_out), .cache_write(and_13_out), .r_dirty(and_2_out),
    .offset(offset), .tag(tag), .RAM_INPUT(RAM_INPUT), .RAM_OUTPUT0(RAM_OUTPUT0), .RAM_OUPUT1(RAM_OUPUT1),
    .RAM_OUTPUT2(RAM_OUTPUT2), .RAM_OUTPUT3(RAM_OUPUT3), .data_in_cache(data_in_cache0),
    .data_read(data_read0), .current_tag(current_tag0), .dirty(dirty0), .DataWrite0(dw00), .DataWrite1(dw10),
    .DataWrite2(dw20), .DataWrite3(dw30), .use_RL(useRL), .update_metadata(and_3_out));
  block_cache block_cache_2 (
    .Clock(Clock), .Reset(Reset), .cache_enable(and_14_out), .cache_write(and_9_out), .r_dirty(and_4_out),
    .offset(offset), .tag(tag), .RAM_INPUT(RAM_INPUT), .RAM_OUTPUT0(RAM_OUTPUT0), .RAM_OUPUT1(RAM_OUPUT1),
    .RAM_OUTPUT2(RAM_OUTPUT2), .RAM_OUTPUT3(RAM_OUPUT3), .data_in_cache(data_in_cache1),
    .data_read(data_read1), .current_tag(current_tag1), .dirty(dirty1), .DataWrite0(dw01), .DataWrite1(dw11),
    .DataWrite2(dw21), .DataWrite3(dw31), .use_RL(useRL), .update_metadata(and_5_out));
  block_cache block_cache_3 (
    .Clock(Clock), .Reset(Reset), .cache_enable(and_15_out), .cache_write(and_10_out), .r_dirty(and_6_out),
    .offset(offset), .tag(tag), .RAM_INPUT(RAM_INPUT), .RAM_OUTPUT0(RAM_OUTPUT0), .RAM_OUPUT1(RAM_OUPUT1),
    .RAM_OUTPUT2(RAM_OUTPUT2), .RAM_OUTPUT3(RAM_OUPUT3), .data_in_cache(data_in_cache2),
    .data_read(data_read2), .current_tag(current_tag2), .dirty(dirty2), .DataWrite0(dw02), .DataWrite1(dw12),
    .DataWrite2(dw22), .DataWrite3(dw32), .use_RL(useRL), .update_metadata(and_7_out));
  block_cache block_cache_4 (
    .Clock(Clock), .Reset(Reset), .cache_enable(and_16_out), .cache_write(and_11_out), .r_dirty(and_1_out),
    .offset(offset), .tag(tag), .RAM_INPUT(RAM_INPUT), .RAM_OUTPUT0(RAM_OUTPUT0), .RAM_OUPUT1(RAM_OUPUT1),
    .RAM_OUTPUT2(RAM_OUTPUT2), .RAM_OUTPUT3(RAM_OUPUT3), .data_in_cache(data_in_cache3),
    .data_read(data_read3), .current_tag(current_tag3), .dirty(dirty3), .DataWrite0(dw03), .DataWrite1(dw13),
    .DataWrite2(dw23), .DataWrite3(dw33), .use_RL(useRL), .update_metadata(and_8_out));
  and and_9 (and_9_out, _1, cache_write);
  and and_10 (and_10_out, _2, cache_write);
  and and_11 (and_11_out, _3, cache_write);
  and and_12 (and_12_out, _0, cache_enable);
  and and_13 (and_13_out, _0, cache_write);
  and and_14 (and_14_out, _1, cache_enable);
  and and_15 (and_15_out, _2, cache_enable);
  and and_16 (and_16_out, _3, cache_enable);
  Decoder #(.select(2), .enable("false")) decoder_1 (.out0(_0), .out1(_1), .out2(_2), .out3(_3), .sel(index));
  Multiplexer #(.select(2), .width(32), .enable("false")) multiplexer_1 (
    .in0(data_read0), .in1(data_read1), .in2(data_read2), .in3(data_read3), .out(data_read), .sel(index));
  Multiplexer #(.select(2), .width(14), .enable("false")) multiplexer_2 (
    .in0(current_tag0), .in1(current_tag1), .in2(current_tag2), .in3(current_tag3), .out(current_tag),
    .sel(index));
  Multiplexer #(.select(2), .width(4), .enable("false")) multiplexer_3 (
    .in0(dirty0), .in1(dirty1), .in2(dirty2), .in3(dirty3), .out(dirty), .sel(index));
  Multiplexer #(.select(2), .width(32), .enable("false")) multiplexer_4 (
    .in0(dw00), .in1(dw01), .in2(dw02), .in3(dw03), .out(DataWrite0), .sel(index));
  Multiplexer #(.select(2), .width(32), .enable("false")) multiplexer_5 (
    .in0(dw10), .in1(dw11), .in2(dw12), .in3(dw13), .out(DataWrite1), .sel(index));
  Multiplexer #(.select(2), .width(32), .enable("false")) multiplexer_6 (
    .in0(dw20), .in1(dw21), .in2(dw22), .in3(dw23), .out(DataWrite2), .sel(index));
  Multiplexer #(.select(2), .width(32), .enable("false")) multiplexer_7 (
    .in0(dw30), .in1(dw31), .in2(dw32), .in3(dw33), .out(DataWrite3), .sel(index));
  Multiplexer #(.select(2), .enable("false")) multiplexer_8 (
    .in0(data_in_cache0), .in1(data_in_cache1), .in2(data_in_cache2), .in3(data_in_cache3),
    .out(data_in_cache), .sel(index));

  // Other names for the same wires on the sheet: CLK = Clock; in_tag[13:0] = tag; RAM_OUTPUT1[31:0] = RAM_OUPUT1;
  //   RAM_OUTPUT3[31:0] = RAM_OUPUT3; RST = Reset
endmodule

module block_cache (
  input  Clock,
  input  Reset,
  input  cache_enable,
  input  cache_write,
  input  r_dirty,
  input  [1:0] offset,
  input  [13:0] tag,
  input  [31:0] RAM_INPUT,
  input  [31:0] RAM_OUTPUT0,
  input  [31:0] RAM_OUPUT1,
  input  [31:0] RAM_OUTPUT2,
  input  [31:0] RAM_OUTPUT3,
  input  use_RL,
  input  update_metadata,
  output data_in_cache,
  output [31:0] data_read,
  output [13:0] current_tag,
  output [3:0] dirty,
  output [31:0] DataWrite0,
  output [31:0] DataWrite1,
  output [31:0] DataWrite2,
  output [31:0] DataWrite3
);

  wire _0, _1, _2, _3, and_1_out, and_2_out, and_3_out, and_4_out, and_5_out, and_6_out, and_7_out,
       and_8_out, data_in_cache0, data_in_cache1, data_in_cache2, data_in_cache3;
  wire [1:0] priority_encoder_1_out, replace_line, working_line;
  wire [3:0] dirty0, dirty1, dirty2, dirty3;
  wire [13:0] current_tag0, current_tag1, current_tag2, current_tag3;
  wire [31:0] data_read0, data_read1, data_read2, data_read3, dw00, dw01, dw02, dw03, dw10, dw11, dw12, dw13,
       dw20, dw21, dw22, dw23, dw30, dw31, dw32, dw33;

  Decoder #(.select(2), .enable("false")) decoder_1 (.out0(_0), .out1(_1), .out2(_2), .out3(_3), .sel(replace_line));
  replacment_policy_lru replacment_policy_lru_1 (
    .in_1(data_in_cache0), .in_2(data_in_cache1), .in_3(data_in_cache2), .in_4(data_in_cache3),
    .update_signal(update_metadata), .clock(Clock), .reset(Reset), .replace_line(replace_line));
  one_line_cache one_line_cache_1 (
    .Clock(Clock), .cache_enable(and_5_out), .offset(offset), .tag(tag), .RAM_OUTPUT0(RAM_OUTPUT0),
    .RAM_OUPUT1(RAM_OUPUT1), .RAM_OUTPUT2(RAM_OUTPUT2), .RAM_OUPUT3(RAM_OUTPUT3), .DataRead(data_read0),
    .data_in_cache(data_in_cache0), .Reset(Reset), .DataWrite0(dw00), .DataWrite1(dw10), .DataWrite2(dw20),
    .DataWrite3(dw30), .RAM_INPUT(RAM_INPUT), .cache_write(and_1_out), .DIRTY(dirty0),
    .current_tag(current_tag0), .r_dirty(r_dirty));
  one_line_cache one_line_cache_2 (
    .Clock(Clock), .cache_enable(and_6_out), .offset(offset), .tag(tag), .RAM_OUTPUT0(RAM_OUTPUT0),
    .RAM_OUPUT1(RAM_OUPUT1), .RAM_OUTPUT2(RAM_OUTPUT2), .RAM_OUPUT3(RAM_OUTPUT3), .DataRead(data_read1),
    .data_in_cache(data_in_cache1), .Reset(Reset), .DataWrite0(dw01), .DataWrite1(dw11), .DataWrite2(dw21),
    .DataWrite3(dw31), .RAM_INPUT(RAM_INPUT), .cache_write(and_2_out), .DIRTY(dirty1),
    .current_tag(current_tag1), .r_dirty(r_dirty));
  one_line_cache one_line_cache_3 (
    .Clock(Clock), .cache_enable(and_7_out), .offset(offset), .tag(tag), .RAM_OUTPUT0(RAM_OUTPUT0),
    .RAM_OUPUT1(RAM_OUPUT1), .RAM_OUTPUT2(RAM_OUTPUT2), .RAM_OUPUT3(RAM_OUTPUT3), .DataRead(data_read2),
    .data_in_cache(data_in_cache2), .Reset(Reset), .DataWrite0(dw02), .DataWrite1(dw12), .DataWrite2(dw22),
    .DataWrite3(dw32), .RAM_INPUT(RAM_INPUT), .cache_write(and_3_out), .DIRTY(dirty2),
    .current_tag(current_tag2), .r_dirty(r_dirty));
  one_line_cache one_line_cache_4 (
    .Clock(Clock), .cache_enable(and_8_out), .offset(offset), .tag(tag), .RAM_OUTPUT0(RAM_OUTPUT0),
    .RAM_OUPUT1(RAM_OUPUT1), .RAM_OUTPUT2(RAM_OUTPUT2), .RAM_OUPUT3(RAM_OUTPUT3), .DataRead(data_read3),
    .data_in_cache(data_in_cache3), .Reset(Reset), .DataWrite0(dw03), .DataWrite1(dw13), .DataWrite2(dw23),
    .DataWrite3(dw33), .RAM_INPUT(RAM_INPUT), .cache_write(and_4_out), .DIRTY(dirty3),
    .current_tag(current_tag3), .r_dirty(r_dirty));
  and and_1 (and_1_out, data_in_cache0, cache_write);
  and and_2 (and_2_out, data_in_cache1, cache_write);
  and and_3 (and_3_out, data_in_cache2, cache_write);
  and and_4 (and_4_out, data_in_cache3, cache_write);
  and and_5 (and_5_out, _0, cache_enable);
  and and_6 (and_6_out, _1, cache_enable);
  and and_7 (and_7_out, _2, cache_enable);
  and and_8 (and_8_out, _3, cache_enable);
  Priority_Encoder #(.select(2)) priority_encoder_1 (
    .in0(data_in_cache0), .in1(data_in_cache1), .in2(data_in_cache2), .in3(data_in_cache3),
    .out(priority_encoder_1_out));  // open: gs, en_out, en_in
  Multiplexer #(.width(2), .enable("false")) multiplexer_1 (
    .in0(priority_encoder_1_out), .in1(replace_line), .out(working_line), .sel(use_RL));
  Multiplexer #(.select(2), .width(32), .enable("false")) multiplexer_2 (
    .in0(dw00), .in1(dw01), .in2(dw02), .in3(dw03), .out(DataWrite0), .sel(working_line));
  Multiplexer #(.select(2), .width(32), .enable("false")) multiplexer_3 (
    .in0(dw10), .in1(dw11), .in2(dw12), .in3(dw13), .out(DataWrite1), .sel(working_line));
  Multiplexer #(.select(2), .width(32), .enable("false")) multiplexer_4 (
    .in0(dw20), .in1(dw21), .in2(dw22), .in3(dw23), .out(DataWrite2), .sel(working_line));
  Multiplexer #(.select(2), .width(32), .enable("false")) multiplexer_5 (
    .in0(dw30), .in1(dw31), .in2(dw32), .in3(dw33), .out(DataWrite3), .sel(working_line));
  or or_1 (data_in_cache, data_in_cache0, data_in_cache1, data_in_cache2, data_in_cache3);
  Multiplexer #(.select(2), .width(32), .enable("false")) multiplexer_6 (
    .in0(data_read0), .in1(data_read1), .in2(data_read2), .in3(data_read3), .out(data_read),
    .sel(working_line));
  Multiplexer #(.select(2), .width(14), .enable("false")) multiplexer_7 (
    .in0(current_tag0), .in1(current_tag1), .in2(current_tag2), .in3(current_tag3), .out(current_tag),
    .sel(working_line));
  Multiplexer #(.select(2), .width(4), .enable("false")) multiplexer_8 (
    .in0(dirty0), .in1(dirty1), .in2(dirty2), .in3(dirty3), .out(dirty), .sel(replace_line));

  // Other names for the same wires on the sheet: CLK = Clock; in_tag[13:0] = tag; RAM_OUTPUT1[31:0] = RAM_OUPUT1;
  //   RST = Reset; useRL = use_RL
endmodule

module one_line_cache (
  input  Clock,
  input  Reset,
  input  cache_enable,
  input  cache_write,
  input  r_dirty,
  input  [1:0] offset,
  input  [13:0] tag,
  input  [31:0] RAM_INPUT,
  input  [31:0] RAM_OUTPUT0,
  input  [31:0] RAM_OUPUT1,
  input  [31:0] RAM_OUTPUT2,
  input  [31:0] RAM_OUPUT3,
  output [31:0] DataRead,
  output [13:0] current_tag,
  output [3:0] DIRTY,
  output [31:0] DataWrite0,
  output data_in_cache,
  output [31:0] DataWrite1,
  output [31:0] DataWrite2,
  output [31:0] DataWrite3
);

  wire and_2_out, and_3_out, and_4_out, and_5_out, comparator_1_eq, or_1_out, or_2_out, or_3_out, or_4_out,
       or_5_out, valid, write0, write1, write2, write3;
  wire [3:0] multiplexer_1_out, NEW_dirty;
  wire [31:0] multiplexer_2_out, multiplexer_3_out, multiplexer_4_out, multiplexer_5_out;

  Demultiplexer #(.select(2), .enable("false")) demultiplexer_1 (
    .out0(write0), .out1(write1), .out2(write2), .out3(write3), .in(1'b1), .sel(offset));
  D_Flip_Flop d_ff_1 (.clk(Clock), .D(1'b1), .Q(valid), .en(cache_enable), .reset(Reset));  // open: Qn, preset
  Register #(.width(14)) register_1 (.D(tag), .en(cache_enable), .Q(current_tag), .clk(Clock), .clr(Reset));
  Multiplexer #(.width(4), .enable("false")) multiplexer_1 (
    .in0(DIRTY), .in1(NEW_dirty), .out(multiplexer_1_out), .sel(cache_write));
  Comparator #(.width(14), .mode("unsigned")) comparator_1 (
    .a(current_tag), .b(tag), .eq(comparator_1_eq));  // open: gt, lt
  Multiplexer #(.width(32), .enable("false")) multiplexer_2 (
    .in0(RAM_OUTPUT0), .in1(RAM_INPUT), .out(multiplexer_2_out), .sel(cache_write));
  Multiplexer #(.width(32), .enable("false")) multiplexer_3 (
    .in0(RAM_OUPUT1), .in1(RAM_INPUT), .out(multiplexer_3_out), .sel(cache_write));
  Multiplexer #(.width(32), .enable("false")) multiplexer_4 (
    .in0(RAM_OUTPUT2), .in1(RAM_INPUT), .out(multiplexer_4_out), .sel(cache_write));
  Multiplexer #(.width(32), .enable("false")) multiplexer_5 (
    .in0(RAM_OUPUT3), .in1(RAM_INPUT), .out(multiplexer_5_out), .sel(cache_write));
  and and_1 (data_in_cache, comparator_1_eq, valid);
  Register #(.width(4)) register_2 (.D(multiplexer_1_out), .Q(DIRTY), .clk(Clock), .clr(or_1_out));  // open: en
  or or_1 (or_1_out, r_dirty, Reset);
  or or_2 (or_2_out, cache_enable, and_2_out);
  and and_2 (and_2_out, cache_write, write0);
  or or_3 (or_3_out, cache_enable, and_3_out);
  and and_3 (and_3_out, cache_write, write1);
  or or_4 (or_4_out, cache_enable, and_4_out);
  and and_4 (and_4_out, cache_write, write2);
  or or_5 (or_5_out, cache_enable, and_5_out);
  and and_5 (and_5_out, cache_write, write3);
  Multiplexer #(.select(2), .width(32), .enable("false")) multiplexer_6 (
    .in0(DataWrite0), .in1(DataWrite1), .in2(DataWrite2), .in3(DataWrite3),
    .out({DataRead[7:0], DataRead[15:8], DataRead[23:16], DataRead[31:24]}), .sel(offset));
  Register #(.width(32)) register_3 (.D(multiplexer_2_out), .en(or_2_out), .Q(DataWrite0), .clk(Clock), .clr(Reset));
  Register #(.width(32)) register_4 (.D(multiplexer_3_out), .en(or_3_out), .Q(DataWrite1), .clk(Clock), .clr(Reset));
  Register #(.width(32)) register_5 (.D(multiplexer_4_out), .en(or_4_out), .Q(DataWrite2), .clk(Clock), .clr(Reset));
  Register #(.width(32)) register_6 (.D(multiplexer_5_out), .en(or_5_out), .Q(DataWrite3), .clk(Clock), .clr(Reset));
  or or_6 (NEW_dirty[0], DIRTY[0], write0);
  or or_7 (NEW_dirty[1], DIRTY[1], write1);
  or or_8 (NEW_dirty[2], DIRTY[2], write2);
  or or_9 (NEW_dirty[3], DIRTY[3], write3);

  // Other names for the same wires on the sheet: cache0[31:0] = DataWrite0; cache1[31:0] = DataWrite1;
  //   cache2[31:0] = DataWrite2; cache3[31:0] = DataWrite3; CLK = Clock; in_tag[13:0] = tag;
  //   RAM_OUTPUT1[31:0] = RAM_OUPUT1; RAM_OUTPUT3[31:0] = RAM_OUPUT3; RST = Reset
endmodule

module replacment_policy_lru (
  input  in_1,
  input  in_2,
  input  in_3,
  input  in_4,
  input  update_signal,
  input  clock,
  input  reset,
  output [1:0] replace_line
);

  wire and_1_out, and_2_out, and_3_out, and_4_out, comparator_1_eq, comparator_2_eq, comparator_3_eq,
       comparator_4_eq, comparator_5_gt, comparator_6_gt, comparator_7_gt, comparator_8_eq, \not , not_1_out,
       not_2_out, not_3_out, not_4_out, S1, S2;
  wire [1:0] controlled_buffer_1_out, meta_data0, meta_data1, meta_data2, meta_data3, multiplexer_1_out,
       multiplexer_2_out, multiplexer_3_out, multiplexer_4_out, multiplexer_5_out, multiplexer_6_out,
       multiplexer_7_out, multiplexer_8_out, multiplexer_12_out, multiplexer_13_out, subtractor_1_out,
       subtractor_2_out, subtractor_3_out, subtractor_4_out;
  wire [1:1] multiplexer_9_out, multiplexer_10_out;

  Subtractor #(.width(2)) subtractor_1 (.a(meta_data0), .b(2'b01), .out(subtractor_1_out));  // open: bin, bout
  Comparator #(.width(2), .mode("unsigned")) comparator_1 (
    .a(meta_data0), .b(2'b00), .eq(comparator_1_eq));  // open: gt, lt
  Subtractor #(.width(2)) subtractor_2 (.a(meta_data1), .b(2'b01), .out(subtractor_2_out));  // open: bin, bout
  Comparator #(.width(2), .mode("unsigned")) comparator_2 (
    .a(meta_data1), .b(2'b00), .eq(comparator_2_eq));  // open: gt, lt
  Subtractor #(.width(2)) subtractor_3 (.a(meta_data2), .b(2'b01), .out(subtractor_3_out));  // open: bin, bout
  Comparator #(.width(2), .mode("unsigned")) comparator_3 (
    .a(meta_data2), .b(2'b00), .eq(comparator_3_eq));  // open: gt, lt
  Subtractor #(.width(2)) subtractor_4 (.a(meta_data3), .b(2'b01), .out(subtractor_4_out));  // open: bin, bout
  Comparator #(.width(2), .mode("unsigned")) comparator_4 (
    .a(meta_data3), .b(2'b00), .eq(comparator_4_eq));  // open: gt, lt
  Multiplexer #(.width(2), .enable("false")) multiplexer_1 (
    .in0(meta_data0), .in1(subtractor_1_out), .out(multiplexer_1_out), .sel(not_1_out));
  not not_1 (not_1_out, comparator_1_eq);
  Multiplexer #(.width(2), .enable("false")) multiplexer_2 (
    .in0(meta_data1), .in1(subtractor_2_out), .out(multiplexer_2_out), .sel(not_2_out));
  not not_2 (not_2_out, comparator_2_eq);
  Multiplexer #(.width(2), .enable("false")) multiplexer_3 (
    .in0(meta_data2), .in1(subtractor_3_out), .out(multiplexer_3_out), .sel(not_3_out));
  not not_3 (not_3_out, comparator_3_eq);
  Multiplexer #(.width(2), .enable("false")) multiplexer_4 (
    .in0(meta_data3), .in1(subtractor_4_out), .out(multiplexer_4_out), .sel(not_4_out));
  not not_4 (not_4_out, comparator_4_eq);
  Multiplexer #(.width(2), .enable("false")) multiplexer_5 (
    .in0(multiplexer_1_out), .in1(2'b11), .out(multiplexer_5_out), .sel(in_1));
  and and_1 (and_1_out, update_signal, \not );
  Multiplexer #(.width(2), .enable("false")) multiplexer_6 (
    .in0(multiplexer_2_out), .in1(2'b11), .out(multiplexer_6_out), .sel(in_2));
  and and_2 (and_2_out, update_signal, \not );
  Multiplexer #(.width(2), .enable("false")) multiplexer_7 (
    .in0(multiplexer_3_out), .in1(2'b11), .out(multiplexer_7_out), .sel(in_3));
  and and_3 (and_3_out, update_signal, \not );
  Multiplexer #(.width(2), .enable("false")) multiplexer_8 (
    .in0(multiplexer_4_out), .in1(2'b11), .out(multiplexer_8_out), .sel(in_4));
  and and_4 (and_4_out, update_signal, \not );
  Register #(.width(2)) register_1 (.D(multiplexer_5_out), .en(and_1_out), .Q(meta_data0), .clk(clock), .clr(reset));
  Register #(.width(2)) register_2 (.D(multiplexer_6_out), .en(and_2_out), .Q(meta_data1), .clk(clock), .clr(reset));
  Register #(.width(2)) register_3 (.D(multiplexer_7_out), .en(and_3_out), .Q(meta_data2), .clk(clock), .clr(reset));
  Register #(.width(2)) register_4 (.D(multiplexer_8_out), .en(and_4_out), .Q(meta_data3), .clk(clock), .clr(reset));
  Comparator #(.width(2), .mode("unsigned")) comparator_5 (
    .a(meta_data0), .b(meta_data1), .gt(comparator_5_gt));  // open: eq, lt
  Comparator #(.width(2), .mode("unsigned")) comparator_6 (
    .a(meta_data2), .b(meta_data3), .gt(comparator_6_gt));  // open: eq, lt
  assign controlled_buffer_1_out = in_1 ? meta_data0 : 2'bz;  // Controlled_Buffer controlled_buffer_1
  Multiplexer #(.width(2), .enable("false")) multiplexer_9 (
    .in0(2'b00), .in1(2'b01), .out({multiplexer_9_out[1], S1}), .sel(comparator_5_gt));
  Multiplexer #(.width(2), .enable("false")) multiplexer_10 (
    .in0(2'b10), .in1(2'b11), .out({multiplexer_10_out[1], S2}), .sel(comparator_6_gt));
  assign controlled_buffer_1_out = in_2 ? meta_data1 : 2'bz;  // Controlled_Buffer controlled_buffer_2
  Multiplexer #(.width(2), .enable("false")) multiplexer_11 (
    .in0({multiplexer_9_out[1], S1}), .in1({multiplexer_10_out[1], S2}), .out(replace_line),
    .sel(comparator_7_gt));
  assign controlled_buffer_1_out = in_3 ? meta_data2 : 2'bz;  // Controlled_Buffer controlled_buffer_3
  Multiplexer #(.width(2), .enable("false")) multiplexer_12 (
    .in0(meta_data0), .in1(meta_data1), .out(multiplexer_12_out), .sel(S1));
  Multiplexer #(.width(2), .enable("false")) multiplexer_13 (
    .in0(meta_data2), .in1(meta_data3), .out(multiplexer_13_out), .sel(S2));
  assign controlled_buffer_1_out = in_4 ? meta_data3 : 2'bz;  // Controlled_Buffer controlled_buffer_4
  Comparator #(.width(2), .mode("unsigned")) comparator_7 (
    .a(multiplexer_12_out), .b(multiplexer_13_out), .gt(comparator_7_gt));  // open: eq, lt
  Comparator #(.width(2), .mode("unsigned")) comparator_8 (
    .a(controlled_buffer_1_out), .b(2'b11), .eq(comparator_8_eq));  // open: gt, lt
  not not_5 (\not , comparator_8_eq);

  // Other names for the same wires on the sheet: _0 = in_1; _1 = in_2; _2 = in_3; _3 = in_4
endmodule

module replacment_policy_random (
  input  CLK,
  input  CACHE_ENABLE,
  output [1:0] REPLACMENT_LINE
);

  wire [1:0] random_1_out;

  Register #(.width(2)) register_1 (.D(random_1_out), .Q(REPLACMENT_LINE), .clk(CLK));  // open: en, clr
  Random #(.width(2)) random_1 (.clk(CLK), .next(CACHE_ENABLE), .out(random_1_out));  // open: clr
endmodule
